# Fritzing sketch raspberry-led (saved by Fritzing 0.9.2b)
breadboards: 1

parts:
  R1 = Resistor [tolerance=±5% resistance=220 package="2010 [SMD]"]
  LED1 = smd LED [color="Red (633nm)" package="0805 [SMD]"]
  Raspberry_Pi-2 = Raspberry Pi 2

nets:
  N1: R1.Pin_0, Raspberry_Pi-2.GND
  N2: R1.Pin_1, LED1.cathode
  N3: LED1.anode, Raspberry_Pi-2.GPIO17
